# Fritzing sketch water pump (saved by Fritzing 0.9.4)

parts:
  Gizwits_WiFi_Witty_ESP-12F1 = Gizwits WiFi Witty ESP-12F
  VCC1 = 4 x AAA Battery Mount
  R1 = PHOTOCELL [package=photocell]
  RHT1 = Humidity and Temperature Sensor RHT03
  Chirp!_Soil_Moisture_Sensor1 = Chirp! Soil Moisture Sensor v2.7.3  # not connected
  WeMos_D1_Mini_Relay_Shield_V1 = WeMos D1 Mini Relay Shield V2
  VCC2 = 4 x AAA Battery Mount
  M1 = DC Motor
  Q1 = NPN-Transistor [package="TO92 [THT]"]
  R2 = Resistor [tolerance=±5% resistance=220 package="0603 [SMD]"]
  R3 = Resistor [tolerance=±5% resistance=220 package="0603 [SMD]"]
  M2 = fc-51 [package=THT]
  IC1 = Voltage Regulator [package=78xxl]

nets:
  N1: Gizwits_WiFi_Witty_ESP-12F1.ADC, R1.P$2, R2.Pin_0
  VCC: Gizwits_WiFi_Witty_ESP-12F1.CH_PD, Gizwits_WiFi_Witty_ESP-12F1.VCC, RHT1.Vcc, R3.Pin_0, IC1.OUT
  N2: Gizwits_WiFi_Witty_ESP-12F1.GPIO0, RHT1.Data-signal, R3.Pin_1
  N3: Gizwits_WiFi_Witty_ESP-12F1.GPIO4, Q1.B
  N4: Gizwits_WiFi_Witty_ESP-12F1.GPIO5, M2.pin1
  N5: VCC1.-, RHT1.GND_1, Q1.C, R2.Pin_1, M2.pin2, IC1.GND
  N6: VCC1.+, R1.P$1, M2.pin3, IC1.IN
  N7: WeMos_D1_Mini_Relay_Shield_V1.COM, VCC2.+
  N8: WeMos_D1_Mini_Relay_Shield_V1.D0, Q1.E
  N9: WeMos_D1_Mini_Relay_Shield_V1.NO, M1.pin_2
  N10: VCC2.-, M1.pin_1
